// Logisim project snake.circ as structural Verilog: 1 circuit, main circuit main
module main (
);

  wire and_1_out, and_2_out, and_3_out, and_4_out, and_5_out, and_6_out, and_7_out, and_8_out, and_9_out,
       and_10_out, and_11_out, and_12_out, and_13_out, and_14_out, and_15_out, and_16_out, and_17_out, Aup,
       available, Bup, CLK, clock_1_out, comparator_1_gt, comparator_2_gt, comparator_3_gt, comparator_4_gt,
       comparator_5_eq, comparator_6_gt, comparator_8_gt, comparator_10_gt, comparator_12_gt,
       comparator_14_eq, comparator_15_eq, comparator_16_eq, comparator_17_eq, comparator_18_eq,
       comparator_19_eq, comparator_20_eq, comparator_21_eq, comparator_22_eq, comparator_23_eq,
       comparator_24_gt, comparator_25_eq, comparator_26_eq, comparator_27_eq, comparator_28_eq,
       comparator_29_eq, comparator_30_eq, comparator_31_eq, comparator_32_eq, comparator_33_lt,
       comparator_34_gt, comparator_35_eq, comparator_36_lt, comparator_37_gt, comparator_38_eq,
       comparator_39_lt, comparator_40_gt, comparator_41_eq, comparator_42_lt, comparator_43_gt,
       comparator_44_eq, comparator_45_lt, comparator_46_gt, comparator_47_eq, comparator_48_lt,
       comparator_49_gt, comparator_50_eq, comparator_51_lt, comparator_52_gt, comparator_53_eq,
       comparator_54_eq, comparator_55_eq, controlled_buffer_1_out, Cup, Dup, multiplexer_6_out, not_1_out,
       not_2_out, not_3_out, not_4_out, not_5_out, not_6_out, or_1_out, or_18_out, or_19_out, or_20_out,
       or_21_out, or_22_out, or_23_out, or_24_out, or_25_out, or_26_out;
  wire [1:0] tunnel;
  wire [3:0] adder_1_out, adder_2_out, adder_3_out, adder_4_out, AppX, AppY, AXPos, AYPos,
       bit_extender_1_out, bit_extender_2_out, bit_extender_7_out, BXPos, BYPos, CXPos, CYPos, direction,
       directionChange, DXPos, DYPos, HeadXPos, HeadYPos, Level, multiplexer_5_out, multiplexer_7_out,
       multiplexer_16_out, multiplexer_25_out, multiplexer_30_out, multiplexer_31_out, Rand0, Rand1, Rand2,
       Rand3, Rand4, Rand5, Rand6, Rand7, random_2_out, RandX, State, subtractor_1_out, subtractor_2_out;
  wire [4:0] bit_extender_3_out, bit_extender_4_out, bit_extender_5_out, bit_extender_6_out,
       multiplexer_17_out, multiplexer_18_out, multiplexer_19_out, multiplexer_20_out;
  wire [6:0] value;
  wire [15:0] _00, _01, _02, _03, _04, _05, _06, _07, _08, _09, _010, _011, _012, _013, _014, _015, A0, A1,
       A2, A3, A4, A5, A6, A7, A8, A9, A10, A11, A12, A13, A14, A15, AYOut, B0, B1, B2, B3, B4, B5, B6, B7,
       B8, B9, B10, B11, B12, B13, B14, B15, BYOut, C0, C1, C2, C3, C4, C5, C6, C7, C8, C9, C10, C11, C12,
       C13, C14, C15, CYOut, D0, D1, D2, D3, D4, D5, D6, D7, D8, D9, D10, D11, D12, D13, D14, D15,
       decoder_6_out0, DYOut, HeadYOut, multiplexer_37_out, multiplexer_38_out, multiplexer_39_out,
       multiplexer_40_out, multiplexer_41_out, multiplexer_42_out, multiplexer_43_out, multiplexer_44_out,
       n0, n1, n2, n3, n4, n5, n6, n7, n8, n9, n10, n11, n12, n13, n14, n15, OR0, OR1, OR2, OR3, OR4, OR5,
       OR6, OR7, OR8, OR9, OR10, OR11, OR12, OR13, OR14, OR15, P0, P1, P2, P3, P4, P5, P6, P7, P8, P9, P10,
       P11, P12, P13, P14, P15, Z0, Z1, Z2, Z3, Z4, Z5, Z6, Z7, Z8, Z9, Z10, Z11, Z12, Z13, Z14, Z15;

  DotMatrix #(.matrixcols(16), .matrixrows(16)) dotmatrix_1 (
    .col0(n0), .col1(n1), .col2(n2), .col3(n3), .col4(n4), .col5(n5), .col6(n6), .col7(n7), .col8(n8),
    .col9(n9), .col10(n10), .col11(n11), .col12(n12), .col13(n13), .col14(n14), .col15(n15));
  Keyboard keyboard_1 (.clk(controlled_buffer_1_out), .avail(available), .data(value));  // open: re, clr
  assign controlled_buffer_1_out = available ? CLK : 1'bz;  // Controlled_Buffer controlled_buffer_1
  Comparator #(.width(4), .mode("unsigned")) comparator_1 (
    .a(State), .b(4'b0001), .gt(comparator_1_gt));  // open: eq, lt
  Comparator #(.width(4), .mode("unsigned")) comparator_2 (
    .a(State), .b(4'b0011), .gt(comparator_2_gt));  // open: eq, lt
  Comparator #(.width(4), .mode("unsigned")) comparator_3 (
    .a(State), .b(4'b0101), .gt(comparator_3_gt));  // open: eq, lt
  Comparator #(.width(4), .mode("unsigned")) comparator_4 (
    .a(State), .b(4'b0111), .gt(comparator_4_gt));  // open: eq, lt
  Hex_Digit_Display hex_digit_display_1 (.value(Level));  // open: dp
  Register #(.width(4)) AY (.D(HeadYPos), .en(comparator_1_gt), .Q(AYPos), .clk(CLK));  // open: clr
  Register #(.width(4)) BY (.D(AYPos), .en(comparator_2_gt), .Q(BYPos), .clk(CLK));  // open: clr
  Register #(.width(4)) CY (.D(BYPos), .en(comparator_3_gt), .Q(CYPos), .clk(CLK));  // open: clr
  Register #(.width(4)) DY (.D(CYPos), .en(comparator_4_gt), .Q(DYPos), .clk(CLK));  // open: clr
  Decoder #(.select(4), .enable("false")) decoder_1 (
    .out0(HeadYOut[0]), .out1(HeadYOut[1]), .out2(HeadYOut[2]), .out3(HeadYOut[3]), .out4(HeadYOut[4]),
    .out5(HeadYOut[5]), .out6(HeadYOut[6]), .out7(HeadYOut[7]), .out8(HeadYOut[8]), .out9(HeadYOut[9]),
    .out10(HeadYOut[10]), .out11(HeadYOut[11]), .out12(HeadYOut[12]), .out13(HeadYOut[13]),
    .out14(HeadYOut[14]), .out15(HeadYOut[15]), .sel(HeadYPos));
  Decoder #(.select(4), .enable("false")) decoder_2 (
    .out0(AYOut[0]), .out1(AYOut[1]), .out2(AYOut[2]), .out3(AYOut[3]), .out4(AYOut[4]), .out5(AYOut[5]),
    .out6(AYOut[6]), .out7(AYOut[7]), .out8(AYOut[8]), .out9(AYOut[9]), .out10(AYOut[10]), .out11(AYOut[11]),
    .out12(AYOut[12]), .out13(AYOut[13]), .out14(AYOut[14]), .out15(AYOut[15]), .sel(AYPos));
  Decoder #(.select(4), .enable("false")) decoder_3 (
    .out0(BYOut[0]), .out1(BYOut[1]), .out2(BYOut[2]), .out3(BYOut[3]), .out4(BYOut[4]), .out5(BYOut[5]),
    .out6(BYOut[6]), .out7(BYOut[7]), .out8(BYOut[8]), .out9(BYOut[9]), .out10(BYOut[10]), .out11(BYOut[11]),
    .out12(BYOut[12]), .out13(BYOut[13]), .out14(BYOut[14]), .out15(BYOut[15]), .sel(BYPos));
  Decoder #(.select(4), .enable("false")) decoder_4 (
    .out0(CYOut[0]), .out1(CYOut[1]), .out2(CYOut[2]), .out3(CYOut[3]), .out4(CYOut[4]), .out5(CYOut[5]),
    .out6(CYOut[6]), .out7(CYOut[7]), .out8(CYOut[8]), .out9(CYOut[9]), .out10(CYOut[10]), .out11(CYOut[11]),
    .out12(CYOut[12]), .out13(CYOut[13]), .out14(CYOut[14]), .out15(CYOut[15]), .sel(CYPos));
  Decoder #(.select(4), .enable("false")) decoder_5 (
    .out0(DYOut[0]), .out1(DYOut[1]), .out2(DYOut[2]), .out3(DYOut[3]), .out4(DYOut[4]), .out5(DYOut[5]),
    .out6(DYOut[6]), .out7(DYOut[7]), .out8(DYOut[8]), .out9(DYOut[9]), .out10(DYOut[10]), .out11(DYOut[11]),
    .out12(DYOut[12]), .out13(DYOut[13]), .out14(DYOut[14]), .out15(DYOut[15]), .sel(DYPos));
  Adder #(.width(4)) adder_1 (.a(bit_extender_2_out), .b(Level), .out(adder_1_out));  // open: cin, cout
  Multiplexer #(.select(4), .width(4), .enable("false")) multiplexer_1 (
    .in0(4'b0000), .in1(4'b0001), .in2(4'b0010), .in3(4'b0011), .in4(4'b0100), .in5(4'b0101), .in6(4'b0110),
    .in7(4'b0111), .in8(4'b1000), .in9(4'b1001), .in10(4'b1010), .in11(4'b1011), .in12(4'b1100),
    .in13(4'b1101), .in14(4'b1110), .in15(4'b1111), .out(Rand0), .sel(RandX));
  Multiplexer #(.select(4), .width(4), .enable("false")) multiplexer_2 (
    .in0(4'b0100), .in1(4'b0101), .in2(4'b0110), .in3(4'b0111), .in4(4'b1000), .in5(4'b1001), .in6(4'b1010),
    .in7(4'b1011), .in8(4'b0100), .in9(4'b0101), .in10(4'b0110), .in11(4'b0111), .in12(4'b1000),
    .in13(4'b1001), .in14(4'b1010), .in15(4'b1011), .out(Rand4), .sel(RandX));
  Register #(.width(4)) u_Level (.D(adder_1_out), .en(1'b1), .Q(Level), .clk(CLK));  // open: clr
  Multiplexer #(.select(4), .width(4), .enable("false")) multiplexer_3 (
    .in0(4'b0001), .in1(4'b0010), .in2(4'b0011), .in3(4'b0100), .in4(4'b0101), .in5(4'b0110), .in6(4'b0111),
    .in7(4'b1000), .in8(4'b1001), .in9(4'b1010), .in10(4'b1011), .in11(4'b1100), .in12(4'b1101),
    .in13(4'b1110), .in14(4'b0011), .in15(4'b1100), .out(Rand1), .sel(RandX));
  Multiplexer #(.select(4), .width(4), .enable("false")) multiplexer_4 (
    .in0(4'b0101), .in1(4'b0110), .in2(4'b0111), .in3(4'b1000), .in4(4'b1001), .in5(4'b1010), .in6(4'b0101),
    .in7(4'b0110), .in8(4'b0111), .in9(4'b1000), .in10(4'b1001), .in11(4'b1010), .in12(4'b0101),
    .in13(4'b0110), .in14(4'b1001), .in15(4'b1010), .out(Rand5), .sel(RandX));
  Register #(.width(4)) u_State (.D(multiplexer_7_out), .en(1'b1), .Q(State), .clk(CLK));  // open: clr
  Random #(.width(4)) random_1 (.clk(CLK), .next(1'b1), .out(RandX));  // open: clr
  Multiplexer #(.select(4), .width(4), .enable("false")) multiplexer_5 (
    .in0(Rand0), .in1(Rand1), .in2(Rand2), .in3(Rand3), .in4(Rand4), .in5(Rand5), .in6(Rand6), .in7(Rand7),
    .out(multiplexer_5_out), .sel(Level));  // open: in8, in9, in10, in11, in12, in13, in14, in15
  Multiplexer #(.select(4), .enable("false")) multiplexer_6 (
    .in0(1'b1), .in1(1'b0), .in2(1'b1), .in3(1'b0), .in4(1'b1), .in5(1'b0), .in6(1'b1), .in7(1'b0),
    .in8(1'b1), .in9(1'b0), .out(multiplexer_6_out), .sel(State));  // open: in10, in11, in12, in13, in14, in15
  Multiplexer #(.width(4), .enable("false")) multiplexer_7 (
    .in0(adder_2_out), .in1(4'b0000), .out(multiplexer_7_out), .sel(comparator_5_eq));
  Multiplexer #(.select(4), .width(4), .enable("false")) multiplexer_8 (
    .in0(4'b0010), .in1(4'b0011), .in2(4'b0100), .in3(4'b0101), .in4(4'b0110), .in5(4'b0111), .in6(4'b1000),
    .in7(4'b1001), .in8(4'b1010), .in9(4'b1011), .in10(4'b1100), .in11(4'b1101), .in12(4'b0011),
    .in13(4'b0101), .in14(4'b1010), .in15(4'b1100), .out(Rand2), .sel(RandX));
  Multiplexer #(.select(4), .width(4), .enable("false")) multiplexer_9 (
    .in0(4'b0110), .in1(4'b0111), .in2(4'b1000), .in3(4'b1001), .in4(4'b0110), .in5(4'b0111), .in6(4'b1000),
    .in7(4'b1001), .in8(4'b0110), .in9(4'b0111), .in10(4'b1000), .in11(4'b1001), .in12(4'b0110),
    .in13(4'b0111), .in14(4'b1000), .in15(4'b1001), .out(Rand6), .sel(RandX));
  assign bit_extender_1_out = {{3{1'b0}}, multiplexer_6_out};  // Bit_Extender bit_extender_1
  Comparator #(.width(4)) comparator_5 (.a(adder_2_out), .b(4'b1010), .eq(comparator_5_eq));  // open: gt, lt
  Multiplexer #(.select(4), .width(4), .enable("false")) multiplexer_10 (
    .in0(4'b0011), .in1(4'b0100), .in2(4'b0101), .in3(4'b0110), .in4(4'b0111), .in5(4'b1000), .in6(4'b1001),
    .in7(4'b1010), .in8(4'b1011), .in9(4'b1100), .in10(4'b0011), .in11(4'b0101), .in12(4'b0111),
    .in13(4'b1000), .in14(4'b1010), .in15(4'b1100), .out(Rand3), .sel(RandX));
  Multiplexer #(.select(4), .width(4), .enable("false")) multiplexer_11 (
    .in0(4'b0111), .in1(4'b1000), .in2(4'b0111), .in3(4'b1000), .in4(4'b0111), .in5(4'b1000), .in6(4'b0111),
    .in7(4'b1000), .in8(4'b0111), .in9(4'b1000), .in10(4'b0111), .in11(4'b1000), .in12(4'b0111),
    .in13(4'b1000), .in14(4'b0111), .in15(4'b1000), .out(Rand7), .sel(RandX));
  Register #(.width(4)) u_AppX (.D(multiplexer_5_out), .en(multiplexer_6_out), .Q(AppX), .clk(CLK));  // open: clr
  Random #(.width(4)) random_2 (.clk(CLK), .next(1'b1), .out(random_2_out));  // open: clr
  Adder #(.width(4)) adder_2 (.a(bit_extender_1_out), .b(State), .out(adder_2_out), .cin(and_1_out));  // open: cout
  assign bit_extender_2_out = {{3{1'b0}}, comparator_5_eq};  // Bit_Extender bit_extender_2
  Register #(.width(4)) u_AppY (.D(random_2_out), .en(multiplexer_6_out), .Q(AppY), .clk(CLK));  // open: clr
  not not_1 (not_1_out, multiplexer_6_out);
  Demultiplexer #(.select(4), .width(16), .enable("false")) demultiplexer_1 (
    .out0(P0), .out1(P1), .out2(P2), .out3(P3), .out4(P4), .out5(P5), .out6(P6), .out7(P7), .out8(P8),
    .out9(P9), .out10(P10), .out11(P11), .out12(P12), .out13(P13), .out14(P14), .out15(P15),
    .in(decoder_6_out0), .sel(AppX));
  Comparator #(.width(4), .mode("unsigned")) comparator_6 (
    .a(State), .b(4'b0111), .gt(comparator_6_gt));  // open: eq, lt
  Comparator #(.width(4), .mode("unsigned")) comparator_7 (.a(State), .b(4'b1000), .gt(Dup));  // open: eq, lt
  Comparator #(.width(4), .mode("unsigned")) comparator_8 (
    .a(State), .b(4'b0101), .gt(comparator_8_gt));  // open: eq, lt
  Comparator #(.width(4), .mode("unsigned")) comparator_9 (.a(State), .b(4'b0110), .gt(Cup));  // open: eq, lt
  Comparator #(.width(4), .mode("unsigned")) comparator_10 (
    .a(State), .b(4'b0011), .gt(comparator_10_gt));  // open: eq, lt
  Comparator #(.width(4), .mode("unsigned")) comparator_11 (.a(State), .b(4'b0100), .gt(Bup));  // open: eq, lt
  Comparator #(.width(4), .mode("unsigned")) comparator_12 (
    .a(State), .b(4'b0001), .gt(comparator_12_gt));  // open: eq, lt
  Comparator #(.width(4), .mode("unsigned")) comparator_13 (.a(State), .b(4'b0010), .gt(Aup));  // open: eq, lt
  Multiplexer #(.select(2), .width(16), .enable("false")) multiplexer_12 (
    .in0(Z0), .in1({16{1'b0}}), .in2({16{1'b0}}), .in3({16{1'b0}}), .out(n0), .sel(tunnel));
  Multiplexer #(.select(2), .width(16), .enable("false")) multiplexer_13 (
    .in0(Z1), .in1(16'h3c0), .in2(16'h3c0), .in3(16'h3c0), .out(n1), .sel(tunnel));
  Multiplexer #(.select(2), .width(16), .enable("false")) multiplexer_14 (
    .in0(Z2), .in1(16'hc30), .in2(16'hc30), .in3(16'hc30), .out(n2), .sel(tunnel));
  Multiplexer #(.select(2), .width(16), .enable("false")) multiplexer_15 (
    .in0(Z3), .in1(16'h1008), .in2(16'h1008), .in3(16'h1008), .out(n3), .sel(tunnel));
  Decoder #(.select(4), .enable("false")) decoder_6 (
    .out0(decoder_6_out0[0]), .out1(decoder_6_out0[1]), .out2(decoder_6_out0[2]), .out3(decoder_6_out0[3]),
    .out4(decoder_6_out0[4]), .out5(decoder_6_out0[5]), .out6(decoder_6_out0[6]), .out7(decoder_6_out0[7]),
    .out8(decoder_6_out0[8]), .out9(decoder_6_out0[9]), .out10(decoder_6_out0[10]),
    .out11(decoder_6_out0[11]), .out12(decoder_6_out0[12]), .out13(decoder_6_out0[13]),
    .out14(decoder_6_out0[14]), .out15(decoder_6_out0[15]), .sel(AppY));
  Comparator #(.width(4)) comparator_14 (.a(HeadXPos), .b(AppX), .eq(comparator_14_eq));  // open: gt, lt
  Comparator #(.width(4)) comparator_15 (.a(HeadYPos), .b(AppY), .eq(comparator_15_eq));  // open: gt, lt
  Register #(.width(4)) CX (.D(CXPos), .en(comparator_6_gt), .Q(DXPos), .clk(CLK));  // open: clr
  Register #(.width(4)) CX_2 (.D(BXPos), .en(comparator_8_gt), .Q(CXPos), .clk(CLK));  // open: clr
  Register #(.width(4)) BX (.D(AXPos), .en(comparator_10_gt), .Q(BXPos), .clk(CLK));  // open: clr
  Register #(.width(4)) AX (.D(HeadXPos), .en(comparator_12_gt), .Q(AXPos), .clk(CLK));  // open: clr
  and and_1 (and_1_out, comparator_14_eq, comparator_15_eq, not_1_out);
  assign bit_extender_3_out = {{1{1'b0}}, DXPos};  // Bit_Extender bit_extender_3
  assign bit_extender_4_out = {{1{1'b0}}, CXPos};  // Bit_Extender bit_extender_4
  assign bit_extender_5_out = {{1{1'b0}}, BXPos};  // Bit_Extender bit_extender_5
  assign bit_extender_6_out = {{1{1'b0}}, AXPos};  // Bit_Extender bit_extender_6
  Multiplexer #(.select(4), .width(4), .enable("false")) multiplexer_16 (
    .in0(4'b0111), .in1(multiplexer_30_out), .in2(multiplexer_30_out), .in3(multiplexer_30_out),
    .in4(multiplexer_30_out), .in5(multiplexer_30_out), .in6(multiplexer_30_out), .in7(multiplexer_30_out),
    .in8(multiplexer_30_out), .in9(multiplexer_30_out), .out(multiplexer_16_out), .sel(State));  // open: in10, in11, in12, in13, in14, in15
  Multiplexer #(.width(5), .enable("false")) multiplexer_17 (
    .in0(5'b10001), .in1(bit_extender_3_out), .out(multiplexer_17_out), .sel(Dup));
  Multiplexer #(.width(5), .enable("false")) multiplexer_18 (
    .in0(5'b10001), .in1(bit_extender_4_out), .out(multiplexer_18_out), .sel(Cup));
  Multiplexer #(.width(5), .enable("false")) multiplexer_19 (
    .in0(5'b10001), .in1(bit_extender_5_out), .out(multiplexer_19_out), .sel(Bup));
  Multiplexer #(.width(5), .enable("false")) multiplexer_20 (
    .in0(5'b10001), .in1(bit_extender_6_out), .out(multiplexer_20_out), .sel(Aup));
  Multiplexer #(.select(2), .width(16), .enable("false")) multiplexer_21 (
    .in0(Z4), .in1(16'h2264), .in2(16'h2434), .in3(16'h2264), .out(n4), .sel(tunnel));
  Multiplexer #(.select(2), .width(16), .enable("false")) multiplexer_22 (
    .in0(Z5), .in1(16'h2414), .in2(16'h2244), .in3(16'h2414), .out(n5), .sel(tunnel));
  Multiplexer #(.select(2), .width(16), .enable("false")) multiplexer_23 (
    .in0(Z6), .in1(16'h4212), .in2(16'h4482), .in3(16'h4212), .out(n6), .sel(tunnel));
  Multiplexer #(.select(2), .width(16), .enable("false")) multiplexer_24 (
    .in0(Z7), .in1(16'h4012), .in2(16'h4082), .in3(16'h4012), .out(n7), .sel(tunnel));
  Register #(.width(4)) HeadX (.D(multiplexer_16_out), .en(1'b1), .Q(HeadXPos), .clk(CLK));  // open: clr
  Register #(.width(4)) HeadY (.D(multiplexer_25_out), .en(1'b1), .Q(HeadYPos), .clk(CLK));  // open: clr
  Multiplexer #(.select(4), .width(4), .enable("false")) multiplexer_25 (
    .in0(4'b1000), .in1(multiplexer_31_out), .in2(multiplexer_31_out), .in3(multiplexer_31_out),
    .in4(multiplexer_31_out), .in5(multiplexer_31_out), .in6(multiplexer_31_out), .in7(multiplexer_31_out),
    .in8(multiplexer_31_out), .in9(multiplexer_31_out), .out(multiplexer_25_out), .sel(State));  // open: in10, in11, in12, in13, in14, in15
  Subtractor #(.width(4)) subtractor_1 (.a(HeadXPos), .b(4'b0001), .out(subtractor_1_out));  // open: bin, bout
  Adder #(.width(4)) adder_3 (.a(HeadXPos), .b(4'b0001), .out(adder_3_out));  // open: cin, cout
  Subtractor #(.width(4)) subtractor_2 (.a(HeadYPos), .b(4'b0001), .out(subtractor_2_out));  // open: bin, bout
  Adder #(.width(4)) adder_4 (.a(HeadYPos), .b(4'b0001), .out(adder_4_out));  // open: cin, cout
  Comparator #(.width(7), .mode("unsigned")) comparator_16 (
    .a(value), .b(7'b1100001), .eq(comparator_16_eq));  // open: gt, lt
  Comparator #(.width(4), .mode("unsigned")) comparator_17 (
    .a(direction), .b(4'b0100), .eq(comparator_17_eq));  // open: gt, lt
  Comparator #(.width(7), .mode("unsigned")) comparator_18 (
    .a(value), .b(7'b1100100), .eq(comparator_18_eq));  // open: gt, lt
  Comparator #(.width(4), .mode("unsigned")) comparator_19 (
    .a(direction), .b(4'b0001), .eq(comparator_19_eq));  // open: gt, lt
  Comparator #(.width(7), .mode("unsigned")) comparator_20 (
    .a(value), .b(7'b1110011), .eq(comparator_20_eq));  // open: gt, lt
  Comparator #(.width(4), .mode("unsigned")) comparator_21 (
    .a(direction), .b(4'b0111), .eq(comparator_21_eq));  // open: gt, lt
  Comparator #(.width(7), .mode("unsigned")) comparator_22 (
    .a(value), .b(7'b1110111), .eq(comparator_22_eq));  // open: gt, lt
  Comparator #(.width(4), .mode("unsigned")) comparator_23 (
    .a(direction), .b(4'b0011), .eq(comparator_23_eq));  // open: gt, lt
  Multiplexer #(.select(2), .width(16), .enable("false")) multiplexer_26 (
    .in0(Z8), .in1(16'h4012), .in2(16'h4082), .in3(16'h4012), .out(n8), .sel(tunnel));
  Multiplexer #(.select(2), .width(16), .enable("false")) multiplexer_27 (
    .in0(Z9), .in1(16'h4212), .in2(16'h4482), .in3(16'h4212), .out(n9), .sel(tunnel));
  Multiplexer #(.select(2), .width(16), .enable("false")) multiplexer_28 (
    .in0(Z10), .in1(16'h2414), .in2(16'h2244), .in3(16'h2414), .out(n10), .sel(tunnel));
  Multiplexer #(.select(2), .width(16), .enable("false")) multiplexer_29 (
    .in0(Z11), .in1(16'h2264), .in2(16'h2434), .in3(16'h2264), .out(n11), .sel(tunnel));
  Multiplexer #(.select(4), .width(4), .enable("false")) multiplexer_30 (
    .in1(subtractor_1_out), .in4(adder_3_out), .out(multiplexer_30_out), .sel(directionChange));  // open: in0, in2, in3, in5, in6, in7, in8, in9, in10, in11, in12, in13, in14, in15
  and and_2 (and_2_out, comparator_16_eq, not_2_out);
  not not_2 (not_2_out, comparator_17_eq);
  and and_3 (and_3_out, comparator_18_eq, not_3_out);
  not not_3 (not_3_out, comparator_19_eq);
  and and_4 (and_4_out, comparator_20_eq, not_4_out);
  not not_4 (not_4_out, comparator_21_eq);
  and and_5 (and_5_out, comparator_22_eq, not_5_out);
  not not_5 (not_5_out, comparator_23_eq);
  Demultiplexer #(.select(5), .width(16), .enable("false")) demultiplexer_2 (
    .out0(D0), .out1(D1), .out2(D2), .out3(D3), .out4(D4), .out5(D5), .out6(D6), .out7(D7), .out8(D8),
    .out9(D9), .out10(D10), .out11(D11), .out12(D12), .out13(D13), .out14(D14), .out15(D15), .in(DYOut),
    .sel(multiplexer_17_out));  // open: out16, out17, out18, out19, out20, out21, out22, out23, out24, out25, out26, out27, out28, out29, out30, out31
  Demultiplexer #(.select(5), .width(16), .enable("false")) demultiplexer_3 (
    .out0(C0), .out1(C1), .out2(C2), .out3(C3), .out4(C4), .out5(C5), .out6(C6), .out7(C7), .out8(C8),
    .out9(C9), .out10(C10), .out11(C11), .out12(C12), .out13(C13), .out14(C14), .out15(C15), .in(CYOut),
    .sel(multiplexer_18_out));  // open: out16, out17, out18, out19, out20, out21, out22, out23, out24, out25, out26, out27, out28, out29, out30, out31
  Demultiplexer #(.select(5), .width(16), .enable("false")) demultiplexer_4 (
    .out0(B0), .out1(B1), .out2(B2), .out3(B3), .out4(B4), .out5(B5), .out6(B6), .out7(B7), .out8(B8),
    .out9(B9), .out10(B10), .out11(B11), .out12(B12), .out13(B13), .out14(B14), .out15(B15), .in(BYOut),
    .sel(multiplexer_19_out));  // open: out16, out17, out18, out19, out20, out21, out22, out23, out24, out25, out26, out27, out28, out29, out30, out31
  Demultiplexer #(.select(5), .width(16), .enable("false")) demultiplexer_5 (
    .out0(A0), .out1(A1), .out2(A2), .out3(A3), .out4(A4), .out5(A5), .out6(A6), .out7(A7), .out8(A8),
    .out9(A9), .out10(A10), .out11(A11), .out12(A12), .out13(A13), .out14(A14), .out15(A15), .in(AYOut),
    .sel(multiplexer_20_out));  // open: out16, out17, out18, out19, out20, out21, out22, out23, out24, out25, out26, out27, out28, out29, out30, out31
  Multiplexer #(.select(4), .width(4), .enable("false")) multiplexer_31 (
    .in3(subtractor_2_out), .in7(adder_4_out), .out(multiplexer_31_out), .sel(directionChange));  // open: in0, in1, in2, in4, in5, in6, in8, in9, in10, in11, in12, in13, in14, in15
  Bit_Extender #(.in_width(7), .out_width(4)) bit_extender_7 (.in(value), .out(bit_extender_7_out));
  Multiplexer #(.select(2), .width(16), .enable("false")) multiplexer_32 (
    .in0(Z12), .in1(16'h1008), .in2(16'h1008), .in3(16'h1008), .out(n12), .sel(tunnel));
  Multiplexer #(.select(2), .width(16), .enable("false")) multiplexer_33 (
    .in0(Z13), .in1(16'hc30), .in2(16'hc30), .in3(16'hc30), .out(n13), .sel(tunnel));
  Multiplexer #(.select(2), .width(16), .enable("false")) multiplexer_34 (
    .in0(Z14), .in1(16'h3c0), .in2(16'h3c0), .in3(16'h3c0), .out(n14), .sel(tunnel));
  Multiplexer #(.select(2), .width(16), .enable("false")) multiplexer_35 (
    .in0(Z15), .in1({16{1'b0}}), .in2({16{1'b0}}), .in3({16{1'b0}}), .out(n15), .sel(tunnel));
  or or_1 (or_1_out, and_2_out, and_3_out, and_4_out, and_5_out);
  Demultiplexer #(.select(4), .width(16), .enable("false")) demultiplexer_6 (
    .out0(_00), .out1(_01), .out2(_02), .out3(_03), .out4(_04), .out5(_05), .out6(_06), .out7(_07),
    .out8(_08), .out9(_09), .out10(_010), .out11(_011), .out12(_012), .out13(_013), .out14(_014),
    .out15(_015), .in(HeadYOut), .sel(HeadXPos));
  Multiplexer #(.width(4), .enable("false")) multiplexer_36 (
    .in0(direction), .in1(bit_extender_7_out), .out(directionChange), .sel(and_6_out));
  and and_6 (and_6_out, or_1_out, available);
  assign OR0 = _00 | A0 | B0 | C0 | D0 | P0;  // OR_Gate or_2, 16 bits wide
  assign OR4 = _04 | A4 | B4 | C4 | D4 | P4;  // OR_Gate or_3, 16 bits wide
  assign OR8 = _08 | A8 | B8 | C8 | D8 | P8;  // OR_Gate or_4, 16 bits wide
  assign OR12 = _012 | A12 | B12 | C12 | D12 | P12;  // OR_Gate or_5, 16 bits wide
  Register #(.width(4)) u_direction (.D(directionChange), .en(1'b1), .Q(direction), .clk(CLK));  // open: clr
  assign OR1 = _01 | A1 | B1 | C1 | D1 | P1;  // OR_Gate or_6, 16 bits wide
  assign OR5 = _05 | A5 | B5 | C5 | D5 | P5;  // OR_Gate or_7, 16 bits wide
  assign OR9 = _09 | A9 | B9 | C9 | D9 | P9;  // OR_Gate or_8, 16 bits wide
  assign OR13 = _013 | A13 | B13 | C13 | D13 | P13;  // OR_Gate or_9, 16 bits wide
  assign OR2 = _02 | A2 | B2 | C2 | D2 | P2;  // OR_Gate or_10, 16 bits wide
  Comparator #(.width(4), .mode("unsigned")) comparator_24 (
    .a(State), .b(4'b0000), .gt(comparator_24_gt));  // open: eq, lt
  assign OR6 = _06 | A6 | B6 | C6 | D6 | P6;  // OR_Gate or_11, 16 bits wide
  assign OR10 = _010 | A10 | B10 | C10 | D10 | P10;  // OR_Gate or_12, 16 bits wide
  assign OR14 = _014 | A14 | B14 | C14 | D14 | P14;  // OR_Gate or_13, 16 bits wide
  assign OR3 = _03 | A3 | B3 | C3 | D3 | P3;  // OR_Gate or_14, 16 bits wide
  assign OR7 = _07 | A7 | B7 | C7 | D7 | P7;  // OR_Gate or_15, 16 bits wide
  assign OR11 = _011 | A11 | B11 | C11 | D11 | P11;  // OR_Gate or_16, 16 bits wide
  assign OR15 = _015 | A15 | B15 | C15 | D15 | P15;  // OR_Gate or_17, 16 bits wide
  Comparator #(.width(4)) comparator_25 (.a(HeadXPos), .b(AXPos), .eq(comparator_25_eq));  // open: gt, lt
  Comparator #(.width(4)) comparator_26 (.a(HeadYPos), .b(AYPos), .eq(comparator_26_eq));  // open: gt, lt
  Comparator #(.width(4)) comparator_27 (.a(HeadXPos), .b(BXPos), .eq(comparator_27_eq));  // open: gt, lt
  Comparator #(.width(4)) comparator_28 (.a(HeadYPos), .b(BYPos), .eq(comparator_28_eq));  // open: gt, lt
  Comparator #(.width(4)) comparator_29 (.a(HeadXPos), .b(CXPos), .eq(comparator_29_eq));  // open: gt, lt
  Comparator #(.width(4)) comparator_30 (.a(HeadYPos), .b(CYPos), .eq(comparator_30_eq));  // open: gt, lt
  Comparator #(.width(4)) comparator_31 (.a(HeadXPos), .b(DXPos), .eq(comparator_31_eq));  // open: gt, lt
  Comparator #(.width(4)) comparator_32 (.a(HeadYPos), .b(DYPos), .eq(comparator_32_eq));  // open: gt, lt
  Comparator #(.width(4), .mode("unsigned")) comparator_33 (
    .a(HeadXPos), .b(4'b0001), .lt(comparator_33_lt));  // open: gt, eq
  Comparator #(.width(4), .mode("unsigned")) comparator_34 (
    .a(HeadXPos), .b(4'b1110), .gt(comparator_34_gt));  // open: eq, lt
  Comparator #(.width(4), .mode("unsigned")) comparator_35 (
    .a(Level), .b(4'b0001), .eq(comparator_35_eq));  // open: gt, lt
  Comparator #(.width(4), .mode("unsigned")) comparator_36 (
    .a(HeadXPos), .b(4'b0010), .lt(comparator_36_lt));  // open: gt, eq
  Comparator #(.width(4), .mode("unsigned")) comparator_37 (
    .a(HeadXPos), .b(4'b1101), .gt(comparator_37_gt));  // open: eq, lt
  Comparator #(.width(4), .mode("unsigned")) comparator_38 (
    .a(Level), .b(4'b0010), .eq(comparator_38_eq));  // open: gt, lt
  Comparator #(.width(4), .mode("unsigned")) comparator_39 (
    .a(HeadXPos), .b(4'b0011), .lt(comparator_39_lt));  // open: gt, eq
  Comparator #(.width(4), .mode("unsigned")) comparator_40 (
    .a(HeadXPos), .b(4'b1100), .gt(comparator_40_gt));  // open: eq, lt
  Comparator #(.width(4), .mode("unsigned")) comparator_41 (
    .a(Level), .b(4'b0011), .eq(comparator_41_eq));  // open: gt, lt
  Comparator #(.width(4), .mode("unsigned")) comparator_42 (
    .a(HeadXPos), .b(4'b0100), .lt(comparator_42_lt));  // open: gt, eq
  Comparator #(.width(4), .mode("unsigned")) comparator_43 (
    .a(HeadXPos), .b(4'b1011), .gt(comparator_43_gt));  // open: eq, lt
  Comparator #(.width(4), .mode("unsigned")) comparator_44 (
    .a(Level), .b(4'b0100), .eq(comparator_44_eq));  // open: gt, lt
  Comparator #(.width(4), .mode("unsigned")) comparator_45 (
    .a(HeadXPos), .b(4'b0101), .lt(comparator_45_lt));  // open: gt, eq
  Comparator #(.width(4), .mode("unsigned")) comparator_46 (
    .a(HeadXPos), .b(4'b1010), .gt(comparator_46_gt));  // open: eq, lt
  Comparator #(.width(4), .mode("unsigned")) comparator_47 (
    .a(Level), .b(4'b0101), .eq(comparator_47_eq));  // open: gt, lt
  Comparator #(.width(4), .mode("unsigned")) comparator_48 (
    .a(HeadXPos), .b(4'b0110), .lt(comparator_48_lt));  // open: gt, eq
  Comparator #(.width(4), .mode("unsigned")) comparator_49 (
    .a(HeadXPos), .b(4'b1001), .gt(comparator_49_gt));  // open: eq, lt
  Comparator #(.width(4), .mode("unsigned")) comparator_50 (
    .a(Level), .b(4'b0110), .eq(comparator_50_eq));  // open: gt, lt
  Comparator #(.width(4), .mode("unsigned")) comparator_51 (
    .a(HeadXPos), .b(4'b0111), .lt(comparator_51_lt));  // open: gt, eq
  Comparator #(.width(4), .mode("unsigned")) comparator_52 (
    .a(HeadXPos), .b(4'b1000), .gt(comparator_52_gt));  // open: eq, lt
  Comparator #(.width(4), .mode("unsigned")) comparator_53 (
    .a(Level), .b(4'b0111), .eq(comparator_53_eq));  // open: gt, lt
  Comparator #(.width(4), .mode("unsigned")) comparator_54 (
    .a(Level), .b(4'b1000), .eq(comparator_54_eq));  // open: gt, lt
  and and_7 (and_7_out, comparator_25_eq, comparator_26_eq, Aup);
  and and_8 (and_8_out, comparator_27_eq, comparator_28_eq, Bup);
  and and_9 (and_9_out, comparator_29_eq, comparator_30_eq, Cup);
  and and_10 (and_10_out, comparator_31_eq, comparator_32_eq, Dup);
  or or_18 (or_18_out, comparator_33_lt, comparator_34_gt);
  or or_19 (or_19_out, comparator_36_lt, comparator_37_gt);
  or or_20 (or_20_out, comparator_39_lt, comparator_40_gt);
  or or_21 (or_21_out, comparator_42_lt, comparator_43_gt);
  or or_22 (or_22_out, comparator_45_lt, comparator_46_gt);
  or or_23 (or_23_out, comparator_48_lt, comparator_49_gt);
  or or_24 (or_24_out, comparator_51_lt, comparator_52_gt);
  and and_11 (and_11_out, or_18_out, comparator_24_gt, comparator_35_eq);
  and and_12 (and_12_out, or_19_out, comparator_24_gt, comparator_38_eq);
  and and_13 (and_13_out, or_20_out, comparator_24_gt, comparator_41_eq);
  and and_14 (and_14_out, or_21_out, comparator_24_gt, comparator_44_eq);
  and and_15 (and_15_out, or_22_out, comparator_24_gt, comparator_47_eq);
  and and_16 (and_16_out, or_23_out, comparator_24_gt, comparator_50_eq);
  and and_17 (and_17_out, or_24_out, comparator_24_gt, comparator_53_eq);
  Comparator #(.width(4), .mode("unsigned")) comparator_55 (
    .a(Level), .b(4'b1000), .eq(comparator_55_eq));  // open: gt, lt
  and and_18 (tunnel[0], comparator_55_eq, tunnel[1]);
  or or_25 (or_25_out, and_7_out, and_8_out, and_9_out, and_10_out, and_11_out, and_12_out, and_13_out, and_14_out, and_15_out, and_16_out, and_17_out, comparator_54_eq);
  Clock clock_1 (.out(clock_1_out));
  and and_19 (CLK, clock_1_out, not_6_out);
  not not_6 (not_6_out, tunnel[1]);
  or or_26 (or_26_out, tunnel[1], or_25_out);
  Register #(.width(1)) register_1 (.D(or_26_out), .en(1'b1), .Q(tunnel[1]), .clk(CLK));  // open: clr
  Multiplexer #(.select(4), .width(16), .enable("false")) multiplexer_37 (
    .in0({16{1'b0}}), .in1({16{1'b1}}), .in2({16{1'b0}}), .in3({16{1'b0}}), .in4({16{1'b0}}),
    .in5({16{1'b0}}), .in6({16{1'b0}}), .in7({16{1'b0}}), .in8({16{1'b0}}), .in9({16{1'b0}}),
    .in10({16{1'b0}}), .in11({16{1'b0}}), .in12({16{1'b0}}), .in13({16{1'b0}}), .in14({16{1'b0}}),
    .in15({16{1'b0}}), .out(multiplexer_37_out), .sel(Level));
  Multiplexer #(.select(4), .width(16), .enable("false")) multiplexer_38 (
    .in0({16{1'b0}}), .in1({16{1'b0}}), .in2({16{1'b1}}), .in3({16{1'b0}}), .in4({16{1'b0}}),
    .in5({16{1'b0}}), .in6({16{1'b0}}), .in7({16{1'b0}}), .in8({16{1'b0}}), .in9({16{1'b0}}),
    .in10({16{1'b0}}), .in11({16{1'b0}}), .in12({16{1'b0}}), .in13({16{1'b0}}), .in14({16{1'b0}}),
    .in15({16{1'b0}}), .out(multiplexer_38_out), .sel(Level));
  Multiplexer #(.select(4), .width(16), .enable("false")) multiplexer_39 (
    .in0({16{1'b0}}), .in1({16{1'b0}}), .in2({16{1'b0}}), .in3({16{1'b1}}), .in4({16{1'b0}}),
    .in5({16{1'b0}}), .in6({16{1'b0}}), .in7({16{1'b0}}), .in8({16{1'b0}}), .in9({16{1'b0}}),
    .in10({16{1'b0}}), .in11({16{1'b0}}), .in12({16{1'b0}}), .in13({16{1'b0}}), .in14({16{1'b0}}),
    .in15({16{1'b0}}), .out(multiplexer_39_out), .sel(Level));
  Multiplexer #(.select(4), .width(16), .enable("false")) multiplexer_40 (
    .in0({16{1'b0}}), .in1({16{1'b0}}), .in2({16{1'b0}}), .in3({16{1'b0}}), .in4({16{1'b1}}),
    .in5({16{1'b0}}), .in6({16{1'b0}}), .in7({16{1'b0}}), .in8({16{1'b0}}), .in9({16{1'b0}}),
    .in10({16{1'b0}}), .in11({16{1'b0}}), .in12({16{1'b0}}), .in13({16{1'b0}}), .in14({16{1'b0}}),
    .in15({16{1'b0}}), .out(multiplexer_40_out), .sel(Level));
  assign Z0 = OR0 | multiplexer_37_out;  // OR_Gate or_27, 16 bits wide
  assign Z15 = multiplexer_37_out | OR15;  // OR_Gate or_28, 16 bits wide
  assign Z1 = OR1 | multiplexer_38_out;  // OR_Gate or_29, 16 bits wide
  assign Z14 = multiplexer_38_out | OR14;  // OR_Gate or_30, 16 bits wide
  assign Z2 = OR2 | multiplexer_39_out;  // OR_Gate or_31, 16 bits wide
  assign Z13 = multiplexer_39_out | OR13;  // OR_Gate or_32, 16 bits wide
  assign Z3 = OR3 | multiplexer_40_out;  // OR_Gate or_33, 16 bits wide
  assign Z12 = multiplexer_40_out | OR12;  // OR_Gate or_34, 16 bits wide
  Multiplexer #(.select(4), .width(16), .enable("false")) multiplexer_41 (
    .in0({16{1'b0}}), .in1({16{1'b0}}), .in2({16{1'b0}}), .in3({16{1'b0}}), .in4({16{1'b0}}),
    .in5({16{1'b1}}), .in6({16{1'b0}}), .in7({16{1'b0}}), .in8({16{1'b0}}), .in9({16{1'b0}}),
    .in10({16{1'b0}}), .in11({16{1'b0}}), .in12({16{1'b0}}), .in13({16{1'b0}}), .in14({16{1'b0}}),
    .in15({16{1'b0}}), .out(multiplexer_41_out), .sel(Level));
  Multiplexer #(.select(4), .width(16), .enable("false")) multiplexer_42 (
    .in0({16{1'b0}}), .in1({16{1'b0}}), .in2({16{1'b0}}), .in3({16{1'b0}}), .in4({16{1'b0}}),
    .in5({16{1'b0}}), .in6({16{1'b1}}), .in7({16{1'b0}}), .in8({16{1'b0}}), .in9({16{1'b0}}),
    .in10({16{1'b0}}), .in11({16{1'b0}}), .in12({16{1'b0}}), .in13({16{1'b0}}), .in14({16{1'b0}}),
    .in15({16{1'b0}}), .out(multiplexer_42_out), .sel(Level));
  Multiplexer #(.select(4), .width(16), .enable("false")) multiplexer_43 (
    .in0({16{1'b0}}), .in1({16{1'b0}}), .in2({16{1'b0}}), .in3({16{1'b0}}), .in4({16{1'b0}}),
    .in5({16{1'b0}}), .in6({16{1'b0}}), .in7({16{1'b1}}), .in8({16{1'b0}}), .in9({16{1'b0}}),
    .in10({16{1'b0}}), .in11({16{1'b0}}), .in12({16{1'b0}}), .in13({16{1'b0}}), .in14({16{1'b0}}),
    .in15({16{1'b0}}), .out(multiplexer_43_out), .sel(Level));
  Multiplexer #(.select(4), .width(16), .enable("false")) multiplexer_44 (
    .in0({16{1'b0}}), .in1({16{1'b0}}), .in2({16{1'b0}}), .in3({16{1'b0}}), .in4({16{1'b0}}),
    .in5({16{1'b0}}), .in6({16{1'b0}}), .in7({16{1'b0}}), .in8({16{1'b1}}), .in9({16{1'b0}}),
    .in10({16{1'b0}}), .in11({16{1'b0}}), .in12({16{1'b0}}), .in13({16{1'b0}}), .in14({16{1'b0}}),
    .in15({16{1'b0}}), .out(multiplexer_44_out), .sel(Level));
  assign Z4 = OR4 | multiplexer_41_out;  // OR_Gate or_35, 16 bits wide
  assign Z11 = multiplexer_41_out | OR11;  // OR_Gate or_36, 16 bits wide
  assign Z5 = OR5 | multiplexer_42_out;  // OR_Gate or_37, 16 bits wide
  assign Z10 = multiplexer_42_out | OR10;  // OR_Gate or_38, 16 bits wide
  assign Z6 = OR6 | multiplexer_43_out;  // OR_Gate or_39, 16 bits wide
  assign Z9 = multiplexer_43_out | OR9;  // OR_Gate or_40, 16 bits wide
  assign Z7 = OR7 | multiplexer_44_out;  // OR_Gate or_41, 16 bits wide
  assign Z8 = multiplexer_44_out | OR8;  // OR_Gate or_42, 16 bits wide

  // Notes on the sheet:
  //   Keyboard
  //   Snake 
  //   by Beetfarm Productions
  //   Game Setup:
  //   1. Enable "Ticks" (suggested 8 Hz)
  //   2. "Poke" keyboard rectangle to enable keyboard input.
  //   Controls:
  //   Gameplay:
  //   Tips
  //   Left, Right, Up, Down = a, d, w, s
  //   Collect apples while avoiding the black columns and your tail.
  //   1. Clock may become erratic if Logism has been active too long.
  //   Completely close, exit and restart Logism to fix the clock.
  //   2. Try to press one key at a time. Pressing too many keys at the same
  //   time or holding keys down may lockup keyboard buffer.
  //   ver 1.0
  //   a=1100001 x61
  //   d=1100100 x64
  //   s=1110011 x73
  //   w=1110111 x77
endmodule
